# Fritzing sketch Sub_Board (saved by Fritzing 0.9.2b)
circuit board: 6.88566cm x 5.36311cm
breadboards: 2

parts:
  J2 = female pin header, 8 pins [form="♀ (female)"]
  J3 = female pin header, 6 pins [form="♀ (female)"]
  J1 = female pin header, 10 pins [form="♀ (female)"]
  J4 = female pin header, 8 pins [form="♀ (female)"]
  J5 = female pin header, 15 pins [form="♀ (female)"]
  J6 = female pin header, 15 pins [form="♀ (female)"]
  Arduino1 = Arduino Uno (Rev3)  # not connected
  J7 = Power Jack [package=power_jack_pth_lock]

nets:
  N1: J2.pin5, J5.pin1, J7.PWR
  N2: J2.pin6, J1.pin4, J5.pin2
  N3: J3.pin1, J6.pin11
  N4: J3.pin2, J5.pin15
  N5: J3.pin5, J6.pin14
  N6: J3.pin6, J6.pin13
  N7: J4.pin2, J6.pin12
  N8: J6.pin2, J7.GND

notes:
  You can send multiple values from the Arduino board to the computer using the serial print function. In this project, the analog values from three potentiometers are used to set the red, green, and blue values of the background color of a Processing sketch running on the computer.
  http://arduino.cc/en/Tutorial/VirtualColorMixer
  TEMP
  CUR
  GND
  5V
  LEDSTRIP
  DAT
  CLK
  A0
  D1
  D2
  D3
  D4
  AMICA R2
  Current & Temp Logger v2
  5V!
